# Fritzing sketch tea_timer_liz (saved by Fritzing 0.9.2b)
breadboards: 1

parts:
  LCD = LCD screen
  POW_JACK = Power Jack [package=power_jack_pth]
  SEL_POT = Rotary Potentiometer (Small) [package=THT]
  SEL_SW = Pushbutton [package="[SMD]"]
  POW_SW = Toggle Switch [package=THT]
  BUZZER = Piezo Speaker
  LCM1602_IIC1 = LCM1602 IIC [part_number="LCM1602 IIC" chip_label="LCM1602 IIC" package="DIP (Dual Inline) [THT]"]
  Part1 = Arduino Uno (Rev3)
  M1 = DC Motor
  D1 = Rectifier Diode [part_number=1N4001 package="Melf DO-213 AB [SMD]"]
  R1 = Resistor [tolerance=±5% resistance=270 package=THT]
  Q1 = NPN-Transistor [package="TO92 [THT]"]
  JACK1 = 2.1mm DC Barrel Jack  # not connected
  JACK2 = 2.1mm Barrel Jack with Terminal Block  # not connected

nets:
  VSS: LCD.VSS, LCM1602_IIC1.VSS
  VDD: LCD.VDD, LCM1602_IIC1.VDD
  N1: LCD.V0, LCM1602_IIC1.V0
  N2: LCD.RS, LCM1602_IIC1.RS
  N3: LCD.R/W, LCM1602_IIC1.RW
  N4: LCD.E, LCM1602_IIC1.E
  N5: LCD.DB0, LCM1602_IIC1.D0
  N6: LCD.DB1, LCM1602_IIC1.D1
  N7: LCD.DB2, LCM1602_IIC1.D2
  N8: LCD.DB3, LCM1602_IIC1.D3
  N9: LCD.DB4, LCM1602_IIC1.D4
  N10: LCD.DB5, LCM1602_IIC1.D5
  N11: LCD.DB6, LCM1602_IIC1.D6
  N12: LCD.DB7, LCM1602_IIC1.D7
  N13: LCD.LED+, LCM1602_IIC1.A
  N14: LCD.LED-, LCM1602_IIC1.K
  GND: POW_JACK.GND, SEL_POT.leg1, SEL_SW.Pin_1, SEL_SW.Pin_2, BUZZER.pin1, LCM1602_IIC1.GND, Part1.GND, Q1.E
  N15: POW_JACK.PWR, POW_SW.COM
  N16: SEL_POT.wiper, Part1.A0
  N17: SEL_SW.Pin_3, SEL_SW.Pin_4, Part1.D2
  VCC: POW_SW.L2, LCM1602_IIC1.VCC, Part1.5V, M1.pin_1, D1.cathode
  N18: BUZZER.pin2, Part1.D8
  N19: LCM1602_IIC1.SDA, Part1.A4/SDA
  N20: LCM1602_IIC1.SCL, Part1.A5/SCL
  N21: Part1.D3_PWM, R1.Pin_1
  N22: M1.pin_2, D1.anode, Q1.C
  N23: R1.Pin_0, Q1.B

custom parts:
  Rotary Potentiometer (Small): A rotary adjustable resistor (potentiometer).
  LCM1602 IIC: I2C-Module to use a 1602 or 2004 LCD on with the wire.h libory Serial LCD Modul
  2.1mm DC Barrel Jack: 2.1mm DC Barrel Jack with Thru-Hole Connectors (breadboardable)
